# Fritzing sketch pico (saved by Fritzing 0.9.6b)

parts:
  Pico_H2 = Raspberry Pi Pico H
  J1 = male pin header, 4 pins [form="♂ (male)"]
  J2 = male pin header, 2 pins [form="♂ (male)"]
  Mod1 = CJMCU-0102
  J3 = male pin header, 2 pins [form="♂ (male)"]
  J4 = male pin header, 4 pins [form="♂ (male)"]
  J5 = male pin header, 4 pins [form="♂ (male)"]  # not connected
  J6 = male pin header, 4 pins [form="♂ (male)"]
  J7 = male pin header, 6 pins [form="♂ (male)"]  # not connected
  J8 = male pin header, 6 pins [form="♂ (male)"]  # not connected

nets:
  GND: Pico_H2.GND, Mod1.GND
  N1: Pico_H2.GP9, J2.pin2
  N2: Pico_H2.GP8, J2.pin1
  N3: Pico_H2.GP2, Mod1.OE
  N4: Pico_H2.GP1, Mod1.A1
  N5: Pico_H2.GP0, Mod1.A2
  N6: J1.pin1, Mod1.B2
  N7: J1.pin2, Mod1.B1
  N8: J1.pin3, Mod1.VB
  N9: J1.pin4, Mod1.G
  N10: Mod1.VA, J3.pin2, J4.pin1, J4.pin2, J4.pin3, J4.pin4, J6.pin1

notes:
  1.8V
  To ROM

custom parts:
  Raspberry Pi Pico H: Raspberry Pi Pico H. Based around the RP2040 microcontroller the Pico H is a low cost microcontroller device bringing Raspberry Pi quality, cost, and easy of use to the microcontroller space.
  CJMCU-0102: 2-Bit Bidirectional Voltage Level Translator I2C IIC Level Module CJMCU-0102 TXS0102.This two-bit non-inverting translator can be used to provide digital switching compatibility between mixed-voltage systems because it is a bidirectional voltage-level translator. The device uses two independent, programmable power supply rails, with the A ports supporting operating voltages between 1.65 V and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
